# Fritzing sketch schematic (saved by Fritzing 0.7.4b)
breadboards: 1

parts:
  Arduino1 = Arduino
  R1 = Resistor [tolerance=±5% resistance=220 package=THT]
  R2 = Resistor [tolerance=±5% resistance=220 package=THT]
  LED1 = LED - 5mm [color="Red (633nm)" package="5 mm [THT]"]
  R3 = Photocell (LDR) [package=THT]

nets:
  N1: Arduino1.D9, R1.Pin_1
  N2: Arduino1.+5V, R2.Pin_0
  N3: Arduino1.GND, LED1.cathode, R3.pin_1
  N4: Arduino1.A0, R2.Pin_1, R3.pin_0
  N5: R1.Pin_0, LED1.anode
